// Logisim project Sub_Circuits_updated_2_Feb.circ as structural Verilog: 4 circuits, main circuit main
module main (
  input  [7:0] in_1,
  input  in_2,
  output [2:0] out_3,
  output [7:0] PC,
  output [13:0] IR,
  output [15:0] Result
);

  wire clock_1_out, not_1_out, shift_register_1_out, shift_register_2_out;
  wire [7:0] MAR_q, R0___R7_datatout, RA_q, ram_1_data, RB_q, RZ_q;
  wire [13:0] rom_1_data;

  Shift_Register #(.length(4)) shift_register_1 (
    .shift(in_2), .in(shift_register_1_out), .clk(clock_1_out), .out(shift_register_1_out));  // open: load, clr, d0, q0, d1, q1, d2, q2, d3, q3
  Program_Counter u_PC (.PC_in(in_1), .Clock(clock_1_out), .PC_Enable(shift_register_2_out), .PCout(PC));
  Clock clock_1 (.out(clock_1_out));
  Register MAR (.D(PC), .en(shift_register_2_out), .Q(MAR_q), .clk(clock_1_out));  // open: clr
  ROM #(.dataWidth(14)) rom_1 (.addr(MAR_q), .data(rom_1_data));  // open: sel
  Shift_Register #(.length(4)) shift_register_2 (
    .shift(in_2), .in(shift_register_2_out), .clk(clock_1_out), .out(shift_register_2_out));  // open: load, clr, d0, q0, d1, q1, d2, q2, d3, q3
  Register #(.width(14)) MBR (.D(rom_1_data), .Q(IR), .clk(clock_1_out));  // open: en, clr
  Reg_File R0___R7 (
    .Datain(RZ_q), .Clock(clock_1_out), .Rx(IR[10:8]), .R_W_prime(shift_register_1_out),
    .DatatOut(R0___R7_datatout));
  Register RA (.D(R0___R7_datatout), .Q(RA_q), .clk(clock_1_out));  // open: en, clr
  not not_1 (not_1_out, shift_register_1_out);
  ALU ALU (.A(RA_q), .B(RB_q), .Operation(IR[13:11]), .Result(Result));
  Register RZ (.D(Result[7:0]), .Q(RZ_q), .clk(clock_1_out));  // open: en, clr
  RAM #(.bus("separate")) ram_1 (
    .addr(IR[7:0]), .din(RB_q), .data(ram_1_data), .str(not_1_out), .clk(clock_1_out),
    .ld(shift_register_1_out));  // open: sel, clr
  Register RB (.D(ram_1_data), .Q(RB_q), .clk(clock_1_out));  // open: en, clr

  assign out_3 = IR[10:8];

  // Notes on the sheet:
  //   Code Mem.
  //   contents of rom_1 (hex, n*v repeats v):
  //   3 901 2202 2b00
  //   Data Mem.
endmodule

module Reg_File (
  input  [7:0] Datain,
  input  Clock,
  input  [2:0] Rx,
  input  R_W_prime,
  output [7:0] DatatOut
);

  wire decoder_1_out0, decoder_1_out1, decoder_1_out2, decoder_1_out3, decoder_1_out4, decoder_1_out5,
       decoder_1_out6, decoder_1_out7, not_1_out;
  wire [7:0] R0_q, R1_q, R2_q, R3_q, R4_q, R5_q, R6_q, R7_q;

  Decoder #(.select(3), .disabled(0)) decoder_1 (
    .out0(decoder_1_out0), .out1(decoder_1_out1), .out2(decoder_1_out2), .out3(decoder_1_out3),
    .out4(decoder_1_out4), .out5(decoder_1_out5), .out6(decoder_1_out6), .out7(decoder_1_out7), .sel(Rx),
    .en(not_1_out));
  not not_1 (not_1_out, R_W_prime);
  Register R0 (.D(Datain), .en(decoder_1_out0), .Q(R0_q), .clk(Clock));  // open: clr
  Register R1 (.D(Datain), .en(decoder_1_out1), .Q(R1_q), .clk(Clock));  // open: clr
  Register R2 (.D(Datain), .en(decoder_1_out2), .Q(R2_q), .clk(Clock));  // open: clr
  Register R3 (.D(Datain), .en(decoder_1_out3), .Q(R3_q), .clk(Clock));  // open: clr
  Register R4 (.D(Datain), .en(decoder_1_out4), .Q(R4_q), .clk(Clock));  // open: clr
  Register R5 (.D(Datain), .en(decoder_1_out5), .Q(R5_q), .clk(Clock));  // open: clr
  Register R6 (.D(Datain), .en(decoder_1_out6), .Q(R6_q), .clk(Clock));  // open: clr
  Register R7 (.D(Datain), .en(decoder_1_out7), .Q(R7_q), .clk(Clock));  // open: clr
  Multiplexer #(.select(3), .width(8)) multiplexer_1 (
    .in0(R0_q), .in1(R1_q), .in2(R2_q), .in3(R3_q), .in4(R4_q), .in5(R5_q), .in6(R6_q), .in7(R7_q),
    .out(DatatOut), .sel(Rx), .en(R_W_prime));
endmodule

module ALU (
  input  [7:0] A,
  input  [7:0] B,
  input  [2:0] Operation,
  output [15:0] Result
);

  wire adder_1_cout, subtractor_1_bout;
  wire [7:0] adder_1_out, and_1_out, bit_extender_1_out, bit_extender_2_out, bit_extender_3_out,
       bit_extender_4_out, bit_extender_5_out, bit_extender_6_out, bit_extender_7_out, divider_1_out,
       divider_1_rem, multiplier_1_cout, multiplier_1_out, or_1_out, subtractor_1_out, xnor_1_out, xor_1_out;

  Adder adder_1 (.a(A), .b(B), .out(adder_1_out), .cout(adder_1_cout));  // open: cin
  Subtractor subtractor_1 (.a(A), .b(B), .out(subtractor_1_out), .bout(subtractor_1_bout));  // open: bin
  Multiplier multiplier_1 (.a(A), .b(B), .out(multiplier_1_out), .cout(multiplier_1_cout));  // open: cin
  Divider divider_1 (.a(A), .b(B), .out(divider_1_out), .rem(divider_1_rem));  // open: upper
  assign and_1_out = A & B;  // AND_Gate and_1, 8 bits wide
  assign or_1_out = A | B;  // OR_Gate or_1, 8 bits wide
  assign xor_1_out = A ^ B;  // XOR_Gate xor_1, 8 bits wide
  assign xnor_1_out = ~(A ^ B);  // XNOR_Gate xnor_1, 8 bits wide
  assign bit_extender_1_out = {{7{1'b0}}, adder_1_cout};  // Bit_Extender bit_extender_1
  assign bit_extender_2_out = {{7{1'b0}}, subtractor_1_bout};  // Bit_Extender bit_extender_2
  Bit_Extender #(.out_width(8)) bit_extender_3 (.in(multiplier_1_cout), .out(bit_extender_3_out));
  assign bit_extender_4_out = {{7{1'b0}}, 1'b0};  // Bit_Extender bit_extender_4
  assign bit_extender_5_out = {{7{1'b0}}, 1'b0};  // Bit_Extender bit_extender_5
  assign bit_extender_6_out = {{7{1'b0}}, 1'b0};  // Bit_Extender bit_extender_6
  assign bit_extender_7_out = {{7{1'b0}}, 1'b0};  // Bit_Extender bit_extender_7
  Multiplexer #(.select(3), .width(16), .enable("false")) multiplexer_1 (
    .in0({bit_extender_1_out, adder_1_out}), .in1({bit_extender_2_out, subtractor_1_out}),
    .in2({bit_extender_3_out, multiplier_1_out}), .in3({divider_1_rem, divider_1_out}),
    .in4({bit_extender_4_out, and_1_out}), .in5({bit_extender_5_out, or_1_out}),
    .in6({bit_extender_6_out, xor_1_out}), .in7({bit_extender_7_out, xnor_1_out}), .out(Result),
    .sel(Operation));
endmodule

module Program_Counter (
  input  [7:0] PC_in,
  input  Clock,
  input  PC_Enable,
  output [7:0] PCout
);

  wire [7:0] adder_1_out;

  Adder adder_1 (.a(PC_in), .b(PCout), .out(adder_1_out), .cin(1'b1));  // open: cout
  Hex_Digit_Display hex_digit_display_1 (.value(PCout[7:4]));  // open: dp
  Register register_1 (.D(adder_1_out), .en(PC_Enable), .Q(PCout), .clk(Clock));  // open: clr
  Hex_Digit_Display hex_digit_display_2 (.value(PCout[3:0]));  // open: dp
endmodule
